// Logisim project ex2.circ as structural Verilog: 1 circuit, main circuit compute_BrUn
module compute_BrUn (
  input  [31:0] INSTRUCTION,
  output BrUn
);

  Comparator #(.width(9)) comparator_1 (
    .a({INSTRUCTION[14:13], INSTRUCTION[6:0]}), .b(9'h1e3), .eq(BrUn));  // open: gt, lt
endmodule
