// Logisim project alu.circ as structural Verilog: 1 circuit, main circuit alu
module alu (
  input  [31:0] A,
  input  [31:0] B,
  input  [3:0] ALUSel,
  output [31:0] ALUResult
);

  wire comparator_1_lt;
  wire [4:0] bit_extender_1_out, bit_extender_2_out, bit_extender_3_out;
  wire [31:0] add0, AND7, MUL8, MULH9, MULHU11, OR6, SLL1, SLT2, SRA13, SRL5, SUB12, XOR4;

  Multiplexer #(.select(4), .width(32)) multiplexer_1 (
    .in0(add0), .in1(SLL1), .in2(SLT2), .in4(XOR4), .in5(SRL5), .in6(OR6), .in7(AND7), .in8(MUL8),
    .in9(MULH9), .in11(MULHU11), .in12(SUB12), .in13(SRA13), .in15(B), .out(ALUResult), .sel(ALUSel));  // open: in3, in10, in14
  Bit_Extender #(.in_width(32), .out_width(5)) bit_extender_1 (.in(B), .out(bit_extender_1_out));
  Bit_Extender #(.in_width(32), .out_width(5)) bit_extender_2 (.in(B), .out(bit_extender_2_out));
  Bit_Extender #(.in_width(32), .out_width(5)) bit_extender_3 (.in(B), .out(bit_extender_3_out));
  Adder #(.width(32)) adder_1 (.a(A), .b(B), .out(add0));  // open: cin, cout
  Shifter #(.width(32)) shifter_1 (.in(A), .\dist (bit_extender_1_out), .out(SLL1));
  Comparator #(.width(32)) comparator_1 (.a(A), .b(B), .lt(comparator_1_lt));  // open: gt, eq
  assign XOR4 = A ^ B;  // XOR_Gate xor_1, 32 bits wide
  Shifter #(.shift("lr"), .width(32)) shifter_2 (.in(A), .\dist (bit_extender_2_out), .out(SRL5));
  assign OR6 = A | B;  // OR_Gate or_1, 32 bits wide
  assign AND7 = A & B;  // AND_Gate and_1, 32 bits wide
  Multiplier #(.mode("twosComplement"), .width(32)) multiplier_1 (.a(A), .b(B), .out(MUL8), .cout(MULH9));  // open: cin
  Multiplier #(.width(32)) multiplier_2 (.a(A), .b(B), .cout(MULHU11));  // open: out, cin
  Subtractor #(.width(32)) subtractor_1 (.a(A), .b(B), .out(SUB12));  // open: bin, bout
  Shifter #(.shift("ar"), .width(32)) shifter_3 (.in(A), .\dist (bit_extender_3_out), .out(SRA13));
  assign SLT2 = {{31{1'b0}}, comparator_1_lt};  // Bit_Extender bit_extender_4

  // Other names for the same wires on the sheet: BSEL15[31:0] = B

  // Notes on the sheet:
  //   INPUTS to your circuit
  //   DON'T CHANGE THE LOCATIONS OF THE INPUTS AND OUTPUTS!
  //   OUTPUT from your circuit
endmodule
